// Logisim project 32-BIT-MIPS.circ as structural Verilog: 13 circuits, main circuit 32-BIT-MIPS
module _32_BIT_MIPS (
  output [31:0] DEBUG
);

  wire ALU_SRC, BRANCH, CLK, clock_1_out, EXTEND, GRT, HALT, JMP, MEM_RD, MEM_TO_REG, MEM_WR, REG_DEST,
       REG_WR, SYSCALL, ZERO;
  wire [2:0] ALU_OP;
  wire [3:0] syscall_control_1_hex0, syscall_control_1_hex1, syscall_control_1_hex2, syscall_control_1_hex3,
       syscall_control_1_hex4, syscall_control_1_hex5, syscall_control_1_hex6, syscall_control_1_hex7;
  wire [4:0] instruction_memory_1_rd_data_1, instruction_memory_1_rd_data_2, instruction_memory_1_wr_reg,
       SHAMT;
  wire [5:0] instruction_memory_1_funct, instruction_memory_1_opcode;
  wire [15:0] instruction_memory_1_immediate;
  wire [31:0] data_memory_1_rd_data, n16_to_32_extend_1_data_out, n32_bit_alu_1_result,
       n32_bit_reg_file_1_data_a, n32_bit_reg_file_1_data_b, pc_logic_1_pc_data, PC_q;

  CONTROL_UNIT control_unit_1 (
    .OPCODE(instruction_memory_1_opcode), .JMP(JMP), .REG_DEST(REG_DEST), .MEM_WR(MEM_WR), .MEM_RD(MEM_RD),
    .MEM_TO_REG(MEM_TO_REG), .REG_WR(REG_WR), .ALU_SRC(ALU_SRC), .EXTEND(EXTEND), .ZERO(ZERO),
    .ALU_OP(ALU_OP), .BRANCH(BRANCH), .GREATER(GRT), .FUNCT(instruction_memory_1_funct), .SYSCALL(SYSCALL));
  Clock clock_1 (.out(clock_1_out));
  Register #(.width(32), .Select("low")) PC (.D(pc_logic_1_pc_data), .Q(PC_q), .clk(CLK));  // open: en, clr
  and and_1 (CLK, ~HALT, clock_1_out);  // AND_Gate
  INSTRUCTION_MEMORY instruction_memory_1 (
    .INSTR_ADDR(PC_q), .WR_REG(instruction_memory_1_wr_reg), .IMMEDIATE(instruction_memory_1_immediate),
    .RD_DATA_2(instruction_memory_1_rd_data_2), .RD_DATA_1(instruction_memory_1_rd_data_1),
    .OPCODE(instruction_memory_1_opcode), ._32_BIT_OUT(DEBUG), .SHAMT(SHAMT),
    .FUNCT(instruction_memory_1_funct));
  PC_LOGIC pc_logic_1 (
    .PC_DATA(pc_logic_1_pc_data), .PC_OUT(PC_q), .OFFSET(n16_to_32_extend_1_data_out), .J_ADDR(DEBUG),
    .BRANCH(BRANCH), .ZERO(ZERO), .JMP(JMP));
  _32_BIT_REG_FILE u_32_bit_reg_file_1 (
    .RD_DATA_2(instruction_memory_1_rd_data_2), .RD_DATA_1(instruction_memory_1_rd_data_1),
    .WR_REG(instruction_memory_1_wr_reg), .DATA_A(n32_bit_reg_file_1_data_a),
    .DATA_B(n32_bit_reg_file_1_data_b), .WR_DATA(data_memory_1_rd_data), .REG_WR(REG_WR),
    .REG_DEST(REG_DEST), .SYSCALL(SYSCALL));
  _16_TO_32_EXTEND u_16_to_32_extend_1 (
    .IMMEDIATE(instruction_memory_1_immediate), .DATA_OUT(n16_to_32_extend_1_data_out), .EXTEND(EXTEND));
  _32_BIT_ALU u_32_bit_alu_1 (
    .A_INPUT(n32_bit_reg_file_1_data_a), .B_INPUT(n32_bit_reg_file_1_data_b), .RESULT(n32_bit_alu_1_result),
    .ALU_OP(ALU_OP), .ZERO(ZERO), .SIGN_EXTEND(n16_to_32_extend_1_data_out), .ALU_SRC(ALU_SRC),
    .GREATER(GRT), .SHAMT(SHAMT));
  DATA_MEMORY data_memory_1 (
    .WR_ADDRESS(n32_bit_alu_1_result), .WR_DATA(n32_bit_reg_file_1_data_b), .RD_DATA(data_memory_1_rd_data),
    .MEM_WR(MEM_WR), .MEM_RD(MEM_RD), .MEM_TO_REG(MEM_TO_REG));
  Hex_Digit_Display hex_digit_display_1 (.value(syscall_control_1_hex0));  // open: dp
  SYSCALL_CONTROL syscall_control_1 (
    .a0(n32_bit_reg_file_1_data_b), .CLK(CLK), .v0(n32_bit_reg_file_1_data_a), .Hex0(syscall_control_1_hex0),
    .Hex1(syscall_control_1_hex1), .Hex2(syscall_control_1_hex2), .Hex3(syscall_control_1_hex3),
    .Hex4(syscall_control_1_hex4), .Hex5(syscall_control_1_hex5), .Hex6(syscall_control_1_hex6), .HALT(HALT),
    .Hex7(syscall_control_1_hex7), .SYSCALL(SYSCALL));  // open: UTF_16
  Hex_Digit_Display hex_digit_display_2 (.value(syscall_control_1_hex2));  // open: dp
  Hex_Digit_Display hex_digit_display_3 (.value(syscall_control_1_hex1));  // open: dp
  Hex_Digit_Display hex_digit_display_4 (.value(syscall_control_1_hex3));  // open: dp
  Hex_Digit_Display hex_digit_display_5 (.value(syscall_control_1_hex4));  // open: dp
  Hex_Digit_Display hex_digit_display_6 (.value(syscall_control_1_hex6));  // open: dp
  Hex_Digit_Display hex_digit_display_7 (.value(syscall_control_1_hex5));  // open: dp
  Hex_Digit_Display hex_digit_display_8 (.value(syscall_control_1_hex7));  // open: dp
endmodule

// GPR
module _32_BIT_ZERO (
  input  DATA_A,
  input  DATA_B,
  output [31:0] DATA_A_2,
  output [31:0] DATA_B_2
);

  assign DATA_A_2 = DATA_A ? {32{1'b0}} : 32'bz;  // Controlled_Buffer controlled_buffer_1
  assign DATA_B_2 = DATA_B ? {32{1'b0}} : 32'bz;  // Controlled_Buffer controlled_buffer_2
endmodule

// GPR
module _32_BIT_REG (
  input  [31:0] DATA_IN,
  input  REG_EN,
  input  DATA_A,
  input  DATA_B,
  output [31:0] DATA_A_2,
  output [31:0] DATA_B_2
);

  wire clock_1_out;
  wire [31:0] REGISTER_q;

  Register #(.width(32), .Select("low")) REGISTER (
    .D(DATA_IN), .en(REG_EN), .Q(REGISTER_q), .clk(clock_1_out));  // open: clr
  Clock clock_1 (.out(clock_1_out));
  assign DATA_A_2 = DATA_A ? REGISTER_q : 32'bz;  // Controlled_Buffer controlled_buffer_1
  assign DATA_B_2 = DATA_B ? REGISTER_q : 32'bz;  // Controlled_Buffer controlled_buffer_2
endmodule

module _32_BIT_REG_FILE (
  input  [4:0] RD_DATA_2,
  input  SYSCALL,
  input  [4:0] RD_DATA_1,
  input  [31:0] WR_DATA,
  input  [4:0] WR_REG,
  input  REG_DEST,
  input  REG_WR,
  output [31:0] DATA_A,
  output [31:0] DATA_B
);

  wire pull_resistor_1_node, pull_resistor_2_node;
  wire [4:0] multiplexer_1_out, multiplexer_2_out, multiplexer_3_out, multiplexer_4_out;
  wire [15:0] DATA_A_out_1, DATA_A_out_2, DATA_B_out_1, DATA_B_out_2, WR_REG_out_1, WR_REG_out_2;

  Multiplexer #(.width(5), .enable("false")) multiplexer_1 (
    .in0(RD_DATA_2), .in1(5'b00100), .out(multiplexer_1_out), .sel(SYSCALL));
  Multiplexer #(.width(5), .enable("false")) multiplexer_2 (
    .in0(RD_DATA_1), .in1(5'b00010), .out(multiplexer_2_out), .sel(SYSCALL));
  Multiplexer #(.width(5), .enable("false")) multiplexer_3 (
    .in0(multiplexer_1_out), .in1(WR_REG), .out(multiplexer_3_out), .sel(REG_DEST));
  Pull_Resistor #(.pull(1)) pull_resistor_1 (.node(pull_resistor_1_node));
  Pull_Resistor #(.pull(1)) pull_resistor_2 (.node(pull_resistor_2_node));
  Multiplexer #(.width(5), .enable("false")) multiplexer_4 (
    .in0(multiplexer_3_out), .in1({5{1'b1}}), .out(multiplexer_4_out), .sel(SYSCALL));
  _5_TO_32_DECODER u_DATA_B (
    .OUT_1(DATA_B_out_1), .OUT_2(DATA_B_out_2), .DEC_OP(multiplexer_1_out), .in_1(pull_resistor_1_node));
  _5_TO_32_DECODER u_DATA_A (
    .OUT_1(DATA_A_out_1), .OUT_2(DATA_A_out_2), .DEC_OP(multiplexer_2_out), .in_1(pull_resistor_2_node));
  _5_TO_32_DECODER u_WR_REG (.OUT_1(WR_REG_out_1), .OUT_2(WR_REG_out_2), .DEC_OP(multiplexer_4_out), .in_1(REG_WR));
  _32_BIT_ZERO ZERO (.DATA_A(DATA_A_out_1[0]), .DATA_B(DATA_B_out_1[0]), .DATA_A_2(DATA_A), .DATA_B_2(DATA_B));
  _32_BIT_REG AT (
    .DATA_IN(WR_DATA), .DATA_A_2(DATA_A), .DATA_B_2(DATA_B), .REG_EN(WR_REG_out_1[1]),
    .DATA_A(DATA_A_out_1[1]), .DATA_B(DATA_B_out_1[1]));
  _32_BIT_REG V0 (
    .DATA_IN(WR_DATA), .DATA_A_2(DATA_A), .DATA_B_2(DATA_B), .REG_EN(WR_REG_out_1[2]),
    .DATA_A(DATA_A_out_1[2]), .DATA_B(DATA_B_out_1[2]));
  _32_BIT_REG V1 (
    .DATA_IN(WR_DATA), .DATA_A_2(DATA_A), .DATA_B_2(DATA_B), .REG_EN(WR_REG_out_1[3]),
    .DATA_A(DATA_A_out_1[3]), .DATA_B(DATA_B_out_1[3]));
  _32_BIT_REG A0 (
    .DATA_IN(WR_DATA), .DATA_A_2(DATA_A), .DATA_B_2(DATA_B), .REG_EN(WR_REG_out_1[4]),
    .DATA_A(DATA_A_out_1[4]), .DATA_B(DATA_B_out_1[4]));
  _32_BIT_REG A1 (
    .DATA_IN(WR_DATA), .DATA_A_2(DATA_A), .DATA_B_2(DATA_B), .REG_EN(WR_REG_out_1[5]),
    .DATA_A(DATA_A_out_1[5]), .DATA_B(DATA_B_out_1[5]));
  _32_BIT_REG A2 (
    .DATA_IN(WR_DATA), .DATA_A_2(DATA_A), .DATA_B_2(DATA_B), .REG_EN(WR_REG_out_1[6]),
    .DATA_A(DATA_A_out_1[6]), .DATA_B(DATA_B_out_1[6]));
  _32_BIT_REG A3 (
    .DATA_IN(WR_DATA), .DATA_A_2(DATA_A), .DATA_B_2(DATA_B), .REG_EN(WR_REG_out_1[7]),
    .DATA_A(DATA_A_out_1[7]), .DATA_B(DATA_B_out_1[7]));
  _32_BIT_REG T0 (
    .DATA_IN(WR_DATA), .DATA_A_2(DATA_A), .DATA_B_2(DATA_B), .REG_EN(WR_REG_out_1[8]),
    .DATA_A(DATA_A_out_1[8]), .DATA_B(DATA_B_out_1[8]));
  _32_BIT_REG T1 (
    .DATA_IN(WR_DATA), .DATA_A_2(DATA_A), .DATA_B_2(DATA_B), .REG_EN(WR_REG_out_1[9]),
    .DATA_A(DATA_A_out_1[9]), .DATA_B(DATA_B_out_1[9]));
  _32_BIT_REG T2 (
    .DATA_IN(WR_DATA), .DATA_A_2(DATA_A), .DATA_B_2(DATA_B), .REG_EN(WR_REG_out_1[10]),
    .DATA_A(DATA_A_out_1[10]), .DATA_B(DATA_B_out_1[10]));
  _32_BIT_REG T3 (
    .DATA_IN(WR_DATA), .DATA_A_2(DATA_A), .DATA_B_2(DATA_B), .REG_EN(WR_REG_out_1[11]),
    .DATA_A(DATA_A_out_1[11]), .DATA_B(DATA_B_out_1[11]));
  _32_BIT_REG T4 (
    .DATA_IN(WR_DATA), .DATA_A_2(DATA_A), .DATA_B_2(DATA_B), .REG_EN(WR_REG_out_1[12]),
    .DATA_A(DATA_A_out_1[12]), .DATA_B(DATA_B_out_1[12]));
  _32_BIT_REG T5 (
    .DATA_IN(WR_DATA), .DATA_A_2(DATA_A), .DATA_B_2(DATA_B), .REG_EN(WR_REG_out_1[13]),
    .DATA_A(DATA_A_out_1[13]), .DATA_B(DATA_B_out_1[13]));
  _32_BIT_REG T6 (
    .DATA_IN(WR_DATA), .DATA_A_2(DATA_A), .DATA_B_2(DATA_B), .REG_EN(WR_REG_out_1[14]),
    .DATA_A(DATA_A_out_1[14]), .DATA_B(DATA_B_out_1[14]));
  _32_BIT_REG T7 (
    .DATA_IN(WR_DATA), .DATA_A_2(DATA_A), .DATA_B_2(DATA_B), .REG_EN(WR_REG_out_1[15]),
    .DATA_A(DATA_A_out_1[15]), .DATA_B(DATA_B_out_1[15]));
  _32_BIT_REG S0 (
    .DATA_IN(WR_DATA), .DATA_A_2(DATA_A), .DATA_B_2(DATA_B), .REG_EN(WR_REG_out_2[0]),
    .DATA_A(DATA_A_out_2[0]), .DATA_B(DATA_B_out_2[0]));
  _32_BIT_REG S1 (
    .DATA_IN(WR_DATA), .DATA_A_2(DATA_A), .DATA_B_2(DATA_B), .REG_EN(WR_REG_out_2[1]),
    .DATA_A(DATA_A_out_2[1]), .DATA_B(DATA_B_out_2[1]));
  _32_BIT_REG S2 (
    .DATA_IN(WR_DATA), .DATA_A_2(DATA_A), .DATA_B_2(DATA_B), .REG_EN(WR_REG_out_2[2]),
    .DATA_A(DATA_A_out_2[2]), .DATA_B(DATA_B_out_2[2]));
  _32_BIT_REG S3 (
    .DATA_IN(WR_DATA), .DATA_A_2(DATA_A), .DATA_B_2(DATA_B), .REG_EN(WR_REG_out_2[3]),
    .DATA_A(DATA_A_out_2[3]), .DATA_B(DATA_B_out_2[3]));
  _32_BIT_REG S4 (
    .DATA_IN(WR_DATA), .DATA_A_2(DATA_A), .DATA_B_2(DATA_B), .REG_EN(WR_REG_out_2[4]),
    .DATA_A(DATA_A_out_2[4]), .DATA_B(DATA_B_out_2[4]));
  _32_BIT_REG S5 (
    .DATA_IN(WR_DATA), .DATA_A_2(DATA_A), .DATA_B_2(DATA_B), .REG_EN(WR_REG_out_2[5]),
    .DATA_A(DATA_A_out_2[5]), .DATA_B(DATA_B_out_2[5]));
  _32_BIT_REG S6 (
    .DATA_IN(WR_DATA), .DATA_A_2(DATA_A), .DATA_B_2(DATA_B), .REG_EN(WR_REG_out_2[6]),
    .DATA_A(DATA_A_out_2[6]), .DATA_B(DATA_B_out_2[6]));
  _32_BIT_REG S7 (
    .DATA_IN(WR_DATA), .DATA_A_2(DATA_A), .DATA_B_2(DATA_B), .REG_EN(WR_REG_out_2[7]),
    .DATA_A(DATA_A_out_2[7]), .DATA_B(DATA_B_out_2[7]));
  _32_BIT_REG T8 (
    .DATA_IN(WR_DATA), .DATA_A_2(DATA_A), .DATA_B_2(DATA_B), .REG_EN(WR_REG_out_2[8]),
    .DATA_A(DATA_A_out_2[8]), .DATA_B(DATA_B_out_2[8]));
  _32_BIT_REG T9 (
    .DATA_IN(WR_DATA), .DATA_A_2(DATA_A), .DATA_B_2(DATA_B), .REG_EN(WR_REG_out_2[9]),
    .DATA_A(DATA_A_out_2[9]), .DATA_B(DATA_B_out_2[9]));
  _32_BIT_REG K0__DNU (
    .DATA_IN(WR_DATA), .DATA_A_2(DATA_A), .DATA_B_2(DATA_B), .REG_EN(WR_REG_out_2[10]),
    .DATA_A(DATA_A_out_2[10]), .DATA_B(DATA_B_out_2[10]));
  _32_BIT_REG K1__DNU (
    .DATA_IN(WR_DATA), .DATA_A_2(DATA_A), .DATA_B_2(DATA_B), .REG_EN(WR_REG_out_2[11]),
    .DATA_A(DATA_A_out_2[11]), .DATA_B(DATA_B_out_2[11]));
  _32_BIT_REG GP (
    .DATA_IN(WR_DATA), .DATA_A_2(DATA_A), .DATA_B_2(DATA_B), .REG_EN(WR_REG_out_2[12]),
    .DATA_A(DATA_A_out_2[12]), .DATA_B(DATA_B_out_2[12]));
  _32_BIT_REG SP (
    .DATA_IN(WR_DATA), .DATA_A_2(DATA_A), .DATA_B_2(DATA_B), .REG_EN(WR_REG_out_2[13]),
    .DATA_A(DATA_A_out_2[13]), .DATA_B(DATA_B_out_2[13]));
  _32_BIT_REG FP (
    .DATA_IN(WR_DATA), .DATA_A_2(DATA_A), .DATA_B_2(DATA_B), .REG_EN(WR_REG_out_2[14]),
    .DATA_A(DATA_A_out_2[14]), .DATA_B(DATA_B_out_2[14]));
  _32_BIT_REG RA (
    .DATA_IN(WR_DATA), .DATA_A_2(DATA_A), .DATA_B_2(DATA_B), .REG_EN(WR_REG_out_2[15]),
    .DATA_A(DATA_A_out_2[15]), .DATA_B(DATA_B_out_2[15]));
  Pull_Resistor pull_resistor_3 (.node(DATA_A));
  Pull_Resistor pull_resistor_4 (.node(DATA_B));
endmodule

module _32_BIT_ALU (
  input  [31:0] A_INPUT,
  input  [4:0] SHAMT,
  input  [2:0] ALU_OP,
  input  [31:0] B_INPUT,
  input  [31:0] SIGN_EXTEND,
  input  ALU_SRC,
  output [31:0] RESULT,
  output ZERO,
  output GREATER
);

  wire comparator_1_lt, not_1_out;
  wire [0:0] multiplexer_2_out;
  wire [31:0] adder_1_out, and_1_out, multiplexer_1_out, or_1_out, shifter_1_out, shifter_2_out,
       subtractor_1_out;

  Multiplexer #(.width(32), .enable("false")) multiplexer_1 (
    .in0(B_INPUT), .in1(SIGN_EXTEND), .out(multiplexer_1_out), .sel(ALU_SRC));
  assign and_1_out = A_INPUT & multiplexer_1_out;  // AND_Gate and_1, 32 bits wide
  assign or_1_out = A_INPUT | multiplexer_1_out;  // OR_Gate or_1, 32 bits wide
  Adder #(.width(32)) adder_1 (.a(A_INPUT), .b(multiplexer_1_out), .out(adder_1_out));  // open: cin, cout
  Shifter #(.width(32)) shifter_1 (.in(A_INPUT), .\dist (SHAMT), .out(shifter_1_out));
  Shifter #(.width(32), .shift("lr")) shifter_2 (.in(A_INPUT), .\dist (SHAMT), .out(shifter_2_out));
  Subtractor #(.width(32)) subtractor_1 (
    .a(A_INPUT), .b(multiplexer_1_out), .out(subtractor_1_out));  // open: bin, bout
  not not_1 (not_1_out, 1'b1);
  Multiplexer #(.enable("false")) multiplexer_2 (
    .in0(not_1_out), .in1(1'b1), .out(multiplexer_2_out[0]), .sel(comparator_1_lt));
  Comparator #(.width(32)) comparator_1 (
    .a(A_INPUT), .b(multiplexer_1_out), .gt(GREATER), .lt(comparator_1_lt));  // open: eq
  Pull_Resistor pull_resistor_1 (.node(RESULT));
  Multiplexer #(.select(3), .width(32), .enable("false")) multiplexer_3 (
    .in0(and_1_out), .in1(or_1_out), .in2(adder_1_out), .in3(shifter_1_out), .in4(shifter_2_out),
    .in6(subtractor_1_out), .in7({{31{1'b0}}, multiplexer_2_out[0]}), .out(RESULT), .sel(ALU_OP));  // open: in5
  Comparator #(.width(32), .mode("unsigned")) comparator_2 (.a(RESULT), .b({32{1'b0}}), .eq(ZERO));  // open: gt, lt
endmodule

module INSTRUCTION_MEMORY (
  input  [31:0] INSTR_ADDR,
  output [5:0] FUNCT,
  output [4:0] SHAMT,
  output [4:0] WR_REG,
  output [15:0] IMMEDIATE,
  output [4:0] RD_DATA_2,
  output [4:0] RD_DATA_1,
  output [5:0] OPCODE,
  output [31:0] _32_BIT_OUT
);

  wire [23:0] bit_extender_1_out;

  Bit_Extender #(.in_width(32), .out_width(24), .\type ("zero")) bit_extender_1 (
    .in(INSTR_ADDR), .out(bit_extender_1_out));
  ROM #(.addrWidth(24), .dataWidth(32), .Select("low")) rom_1 (.addr(bit_extender_1_out), .data(_32_BIT_OUT));
  Pull_Resistor pull_resistor_1 (.node(_32_BIT_OUT));

  assign FUNCT = _32_BIT_OUT[5:0];
  assign IMMEDIATE = _32_BIT_OUT[15:0];
  assign OPCODE = _32_BIT_OUT[31:26];
  assign RD_DATA_1 = _32_BIT_OUT[25:21];
  assign RD_DATA_2 = _32_BIT_OUT[20:16];
  assign SHAMT = _32_BIT_OUT[10:6];
  assign WR_REG = _32_BIT_OUT[15:11];

  // Notes on the sheet:
  //   contents of rom_1 (hex, n*v repeats v):
  //   34080064 34090014 1092020 20020001 c
endmodule

module DATA_MEMORY (
  input  [31:0] WR_ADDRESS,
  input  [31:0] WR_DATA,
  input  MEM_WR,
  input  MEM_RD,
  input  MEM_TO_REG,
  output [31:0] RD_DATA
);

  wire clock_1_out;
  wire [23:0] bit_extender_1_out;
  wire [31:0] ram_1_data;

  Bit_Extender #(.in_width(32), .out_width(24), .\type ("zero")) bit_extender_1 (
    .in(WR_ADDRESS), .out(bit_extender_1_out));
  RAM #(.addrWidth(24), .dataWidth(32), .bus("separate"), .Select("low")) ram_1 (
    .addr(bit_extender_1_out), .din(WR_DATA), .data(ram_1_data), .str(MEM_WR), .clk(clock_1_out), .ld(MEM_RD));  // open: sel, clr
  Clock clock_1 (.out(clock_1_out));
  Multiplexer #(.width(32), .enable("false")) multiplexer_1 (
    .in0(WR_ADDRESS), .in1(ram_1_data), .out(RD_DATA), .sel(MEM_TO_REG));
endmodule

module SYSCALL_CONTROL (
  input  [31:0] a0,
  input  CLK,
  input  SYSCALL,
  input  [31:0] v0,
  output [15:0] UTF_16,
  output [3:0] Hex0,
  output [3:0] Hex1,
  output [3:0] Hex2,
  output [3:0] Hex3,
  output [3:0] Hex4,
  output [3:0] Hex5,
  output [3:0] Hex6,
  output [3:0] Hex7,
  output HALT
);

  wire and_1_out, and_2_out, comparator_1_eq, comparator_2_eq, comparator_3_eq, multiplexer_1_out, or_1_out;
  wire [31:0] multiplexer_2_out, pull_resistor_1_node;

  and and_1 (and_1_out, comparator_2_eq, SYSCALL);
  Comparator #(.width(32)) comparator_1 (.a(v0), .b(32'ha), .eq(comparator_1_eq));  // open: gt, lt
  Comparator #(.width(32)) comparator_2 (.a(v0), .b(32'h1), .eq(comparator_2_eq));  // open: gt, lt
  Comparator #(.width(32)) comparator_3 (.a(v0), .b(32'h4), .eq(comparator_3_eq));  // open: gt, lt
  or or_1 (or_1_out, and_1_out, and_2_out);
  and and_2 (and_2_out, comparator_3_eq, SYSCALL);
  Register #(.width(32), .Select("low")) THING (
    .D(a0), .en(or_1_out), .Q({Hex0, Hex1, Hex2, Hex3, Hex4, Hex5, Hex6, Hex7}), .clk(CLK));  // open: clr
  Multiplexer #(.enable("false")) multiplexer_1 (
    .in0(1'b0), .in1(comparator_1_eq), .out(multiplexer_1_out), .sel(SYSCALL));
  Pull_Resistor pull_resistor_1 (.node(pull_resistor_1_node));
  Multiplexer #(.width(32), .disabled(0), .enable("false")) multiplexer_2 (
    .in0(pull_resistor_1_node), .in1({Hex0, Hex1, Hex2, Hex3, Hex4, Hex5, Hex6, Hex7}),
    .out(multiplexer_2_out), .sel(comparator_3_eq));
  D_Flip_Flop #(.Pre_Clr_Positions("LEGACY"), .enable("true"), .NewFFLayout("false")) d_ff_1 (
    .clk(CLK), .D(multiplexer_1_out), .Q(HALT));  // open: Qn, preset, en, reset
  Bit_Extender #(.in_width(32), .\type ("zero")) bit_extender_1 (.in(multiplexer_2_out), .out(UTF_16));

  // Notes on the sheet:
  //   EXIT
  //   PRINT INT
  //   PRINT STRING
endmodule

module CONTROL_UNIT (
  input  [5:0] FUNCT,
  input  [5:0] OPCODE,
  input  ZERO,
  input  GREATER,
  output SYSCALL,
  output BRANCH,
  output JMP,
  output REG_DEST,
  output MEM_WR,
  output MEM_RD,
  output MEM_TO_REG,
  output REG_WR,
  output ALU_SRC,
  output EXTEND,
  output [2:0] ALU_OP
);

  wire ADD_out, ADDI_out, ADDIU_out, and_2_out, and_3_out, and_4_out, AND_5_out, ANDI_out, BEQ_out, BGTZ_out,
       BNE_out, or_1_out, or_2_out, OR_4_out, ORI_out, SLL_out, SLT_out, SLTI_out, SRL_out, SUB_out,
       SYSCALL_out;
  wire [3:0] priority_encoder_1_out;
  wire [5:0] multiplexer_1_out;

  and R_type (REG_DEST, ~OPCODE[5], ~OPCODE[4], ~OPCODE[3], ~OPCODE[2], ~OPCODE[1], ~OPCODE[0]);  // AND_Gate
  and LW (MEM_RD, OPCODE[5], ~OPCODE[4], ~OPCODE[3], ~OPCODE[2], OPCODE[1], OPCODE[0]);  // AND_Gate
  and SW (MEM_WR, OPCODE[5], ~OPCODE[4], OPCODE[3], ~OPCODE[2], OPCODE[1], OPCODE[0]);  // AND_Gate
  and BEQ (BEQ_out, ~OPCODE[5], ~OPCODE[4], ~OPCODE[3], OPCODE[2], ~OPCODE[1], ~OPCODE[0]);  // AND_Gate
  and ADDI (ADDI_out, ~OPCODE[5], ~OPCODE[4], OPCODE[3], ~OPCODE[2], ~OPCODE[1], ~OPCODE[0]);  // AND_Gate
  and SLTI (SLTI_out, ~OPCODE[5], ~OPCODE[4], OPCODE[3], ~OPCODE[2], OPCODE[1], ~OPCODE[0]);  // AND_Gate
  and ANDI (ANDI_out, ~OPCODE[5], ~OPCODE[4], OPCODE[3], OPCODE[2], ~OPCODE[1], ~OPCODE[0]);  // AND_Gate
  or or_1 (or_1_out, BNE_out, BGTZ_out, BEQ_out);
  and ORI (ORI_out, ~OPCODE[5], ~OPCODE[4], OPCODE[3], OPCODE[2], ~OPCODE[1], OPCODE[0]);  // AND_Gate
  and J (JMP, ~OPCODE[5], ~OPCODE[4], ~OPCODE[3], ~OPCODE[2], OPCODE[1], ~OPCODE[0]);  // AND_Gate
  and BNE (BNE_out, ~OPCODE[5], ~OPCODE[4], ~OPCODE[3], OPCODE[2], ~OPCODE[1], OPCODE[0]);  // AND_Gate
  and BGTZ (BGTZ_out, ~OPCODE[5], ~OPCODE[4], ~OPCODE[3], OPCODE[2], OPCODE[1], OPCODE[0]);  // AND_Gate
  and u_SYSCALL (SYSCALL_out, ~FUNCT[5], ~FUNCT[4], FUNCT[3], FUNCT[2], ~FUNCT[1], ~FUNCT[0]);  // AND_Gate
  and ADDIU (ADDIU_out, ~OPCODE[5], ~OPCODE[4], OPCODE[3], ~OPCODE[2], ~OPCODE[1], OPCODE[0]);  // AND_Gate
  nor nor_1 (ALU_SRC, BGTZ_out, BNE_out, REG_DEST);
  not nor_2 (EXTEND, ADDIU_out);  // NOR_Gate
  or or_2 (or_2_out, ADDIU_out, ADDI_out, MEM_WR, MEM_RD);
  Priority_Encoder #(.select(4)) priority_encoder_1 (
    .in0(or_2_out), .in4(ANDI_out), .in5(ORI_out), .in6(or_1_out), .in10(SLTI_out),
    .out(priority_encoder_1_out));  // open: in1, in2, in3, in7, in8, in9, in11, in12, in13, in14, in15, gs, en_out, en_in
  and and_1 (SYSCALL, SYSCALL_out, REG_DEST);
  or RegWrite (REG_WR, ADDIU_out, ORI_out, ANDI_out, SLTI_out, ADDI_out, MEM_RD, REG_DEST);
  Pull_Resistor pull_resistor_1 (.node(priority_encoder_1_out));
  or or_3 (BRANCH, and_2_out, and_3_out, and_4_out);
  and and_2 (and_2_out, BGTZ_out, GREATER);
  and and_3 (and_3_out, ~ZERO, BNE_out);  // AND_Gate
  Multiplexer #(.width(6), .disabled(0), .enable("false")) multiplexer_1 (
    .in0({2'b10, priority_encoder_1_out}), .in1(FUNCT), .out(multiplexer_1_out), .sel(REG_DEST));
  and and_4 (and_4_out, ZERO, BEQ_out);
  and ADD (ADD_out, ~multiplexer_1_out[0], ~multiplexer_1_out[1], ~multiplexer_1_out[2], ~multiplexer_1_out[3], ~multiplexer_1_out[4], multiplexer_1_out[5]);  // AND_Gate
  Priority_Encoder priority_encoder_2 (
    .in0(AND_5_out), .in1(OR_4_out), .in2(ADD_out), .in3(SLL_out), .in4(SRL_out), .in6(SUB_out),
    .in7(SLT_out), .out(ALU_OP));  // open: in5, gs, en_out, en_in
  and SUB (SUB_out, ~multiplexer_1_out[0], multiplexer_1_out[1], multiplexer_1_out[2], ~multiplexer_1_out[3], ~multiplexer_1_out[4], multiplexer_1_out[5]);  // AND_Gate
  and AND_5 (AND_5_out, ~multiplexer_1_out[0], ~multiplexer_1_out[1], multiplexer_1_out[2], ~multiplexer_1_out[3], ~multiplexer_1_out[4], multiplexer_1_out[5]);  // AND_Gate
  and OR_4 (OR_4_out, multiplexer_1_out[0], ~multiplexer_1_out[1], multiplexer_1_out[2], ~multiplexer_1_out[3], ~multiplexer_1_out[4], multiplexer_1_out[5]);  // AND_Gate
  and SLT (SLT_out, ~multiplexer_1_out[0], multiplexer_1_out[1], ~multiplexer_1_out[2], multiplexer_1_out[3], ~multiplexer_1_out[4], multiplexer_1_out[5]);  // AND_Gate
  and SLL (SLL_out, ~multiplexer_1_out[0], ~multiplexer_1_out[1], ~multiplexer_1_out[2], ~multiplexer_1_out[3], ~multiplexer_1_out[4], ~multiplexer_1_out[5]);  // AND_Gate
  and SRL (SRL_out, multiplexer_1_out[0], multiplexer_1_out[1], multiplexer_1_out[2], multiplexer_1_out[3], ~multiplexer_1_out[4], multiplexer_1_out[5]);  // AND_Gate

  assign MEM_TO_REG = MEM_RD;
endmodule

module JUMP_CONTROL (
  input  [31:0] DATA_IN,
  input  [31:0] PC_COUNT_IN,
  output [31:0] DATA_OUT
);

  wire [25:0] bit_extender_1_out, shifter_1_out;

  Bit_Extender #(.in_width(32), .out_width(26), .\type ("zero")) bit_extender_1 (
    .in(DATA_IN), .out(bit_extender_1_out));
  Shifter #(.width(26)) shifter_1 (.in(bit_extender_1_out), .\dist (5'b00010), .out(shifter_1_out));
  assign DATA_OUT[27:0] = {{2{1'b0}}, shifter_1_out};  // Bit_Extender bit_extender_2

  assign DATA_OUT[31:28] = PC_COUNT_IN[31:28];
endmodule

module PC_LOGIC (
  input  [31:0] PC_OUT,
  input  [31:0] OFFSET,
  input  [31:0] J_ADDR,
  input  BRANCH,
  input  ZERO,
  input  JMP,
  output [31:0] PC_DATA
);

  wire and_1_out;
  wire [31:0] adder_1_out, adder_2_out, jump_control_1_data_out, multiplexer_1_out, shifter_1_out;

  Adder #(.width(32)) adder_1 (.a(32'h1), .b(PC_OUT), .out(adder_1_out));  // open: cin, cout
  Shifter #(.width(32)) shifter_1 (.in(OFFSET), .\dist (5'b00010), .out(shifter_1_out));
  JUMP_CONTROL jump_control_1 (.DATA_IN(J_ADDR), .PC_COUNT_IN(adder_1_out), .DATA_OUT(jump_control_1_data_out));
  Multiplexer #(.width(32), .enable("false")) multiplexer_1 (
    .in0(adder_1_out), .in1(adder_2_out), .out(multiplexer_1_out), .sel(and_1_out));
  Adder #(.width(32)) adder_2 (.a(adder_1_out), .b(shifter_1_out), .out(adder_2_out));  // open: cin, cout
  and and_1 (and_1_out, BRANCH, ZERO);
  Multiplexer #(.width(32), .enable("false")) multiplexer_2 (
    .in0(multiplexer_1_out), .in1(jump_control_1_data_out), .out(PC_DATA), .sel(JMP));
endmodule

module _5_TO_32_DECODER (
  input  in_1,
  input  [4:0] DEC_OP,
  output [15:0] OUT_1,
  output [15:0] OUT_2
);

  Demultiplexer #(.select(5), .enable("false")) demultiplexer_1 (
    .out0(OUT_1[0]), .out1(OUT_1[1]), .out2(OUT_1[2]), .out3(OUT_1[3]), .out4(OUT_1[4]), .out5(OUT_1[5]),
    .out6(OUT_1[6]), .out7(OUT_1[7]), .out8(OUT_1[8]), .out9(OUT_1[9]), .out10(OUT_1[10]), .out11(OUT_1[11]),
    .out12(OUT_1[12]), .out13(OUT_1[13]), .out14(OUT_1[14]), .out15(OUT_1[15]), .out16(OUT_2[0]),
    .out17(OUT_2[1]), .out18(OUT_2[2]), .out19(OUT_2[3]), .out20(OUT_2[4]), .out21(OUT_2[5]),
    .out22(OUT_2[6]), .out23(OUT_2[7]), .out24(OUT_2[8]), .out25(OUT_2[9]), .out26(OUT_2[10]),
    .out27(OUT_2[11]), .out28(OUT_2[12]), .out29(OUT_2[13]), .out30(OUT_2[14]), .out31(OUT_2[15]), .in(in_1),
    .sel(DEC_OP));
endmodule

module _16_TO_32_EXTEND (
  input  [15:0] IMMEDIATE,
  input  EXTEND,
  output [31:0] DATA_OUT
);

  wire [31:0] bit_extender_1_out, bit_extender_2_out;

  assign bit_extender_1_out = {{16{1'b0}}, IMMEDIATE};  // Bit_Extender bit_extender_1
  assign bit_extender_2_out = {{16{IMMEDIATE[15]}}, IMMEDIATE};  // Bit_Extender bit_extender_2
  Multiplexer #(.width(32), .enable("false")) multiplexer_1 (
    .in0(bit_extender_1_out), .in1(bit_extender_2_out), .out(DATA_OUT), .sel(EXTEND));
endmodule
